// Logisim project IT012_Lab01_25521178.circ as structural Verilog: 5 circuits, main circuit TN2
module TN1 (
  input  A,
  input  B,
  input  C,
  output out_4,
  output AND,
  output OR,
  output NOR,
  output CHAIN,
  output XOR,
  output NXOR,
  output XOR3,
  output NAND_3
);

  wire NAND_out;

  not not_1 (out_4, A);
  and and_1 (AND, A, B);
  or or_1 (OR, A, B);
  nand NAND (NAND_out, A, B);
  nor nor_1 (NOR, A, B);
  xor xor_1 (XOR, A, B);
  xnor xnor_1 (NXOR, A, B);
  ExactlyOne xor_2 (.out(XOR3), .in0(A), .in1(B), .in2(C));
  nand nand_2 (NAND_3, A, B, C);
  nand u_nand_3 (CHAIN, NAND_out, C);
endmodule

module TN2 (
  input  x,
  input  y,
  input  z,
  output out_4,
  output out_5,
  output out_6,
  output out_7,
  output out_8
);

  wire not_1_out, not_2_out, not_3_out, x___x_prime_y_out, x___y_2_out, x___y__prime_out, x___y__x___z_out,
       x___y_out, x___yz_out, x___z_out, x_prime_y_out, x_prime_y_prime_out, xy__prime_out, yz_out;

  not not_1 (not_1_out, x);
  not not_2 (not_2_out, y);
  not not_3 (not_3_out, x);
  and x_prime_y_prime (x_prime_y_prime_out, not_1_out, not_2_out);
  nand xy__prime (xy__prime_out, x, y);
  and yz (yz_out, y, z);
  or x___y (x___y_out, x, y);
  or x___z (x___z_out, x, z);
  and x_prime_y (x_prime_y_out, not_3_out, y);
  nor x___y__prime (x___y__prime_out, x, y);
  or x___yz (x___yz_out, yz_out, x);
  and x___y__x___z (x___y__x___z_out, x___y_out, x___z_out);
  or x___x_prime_y (x___x_prime_y_out, x, x_prime_y_out);
  or x___y_2 (x___y_2_out, x, y);
  xnor EQ1 (out_4, x___y__prime_out, x_prime_y_prime_out);
  xnor EQ2 (out_5, x_prime_y_prime_out, xy__prime_out);
  xnor EQ3 (out_6, x___yz_out, x___y__x___z_out);
  xnor EQ4 (out_7, x, x___x_prime_y_out);
  xnor EQ5 (out_8, x___x_prime_y_out, x___y_2_out);
endmodule

module TN3 (
  input  A,
  input  B,
  input  C,
  input  in_4,
  output out_5
);

  wire and_1_out, and_2_out, and_3_out, and_4_out, and_5_out, and_6_out, not_1_out, not_2_out, not_3_out,
       not_4_out;

  not not_1 (not_1_out, A);
  not not_2 (not_2_out, B);
  not not_3 (not_3_out, C);
  not not_4 (not_4_out, in_4);
  and and_1 (and_1_out, not_1_out, not_2_out, C, not_4_out);
  and and_2 (and_2_out, not_1_out, not_2_out, C, in_4);
  and and_3 (and_3_out, not_1_out, B, not_3_out, in_4);
  and and_4 (and_4_out, not_1_out, B, C, in_4);
  and and_5 (and_5_out, A, not_2_out, C, in_4);
  and and_6 (and_6_out, A, B, not_3_out, in_4);
  or or_1 (out_5, and_1_out, and_2_out, and_3_out, and_4_out, and_5_out, and_6_out);
endmodule

module TN4 (
  input  A,
  input  B,
  input  C,
  input  D,
  output F_can,
  output EQ1,
  output F_sop,
  output EQ2,
  output F_pos
);

  wire and_1_out, and_2_out, and_3_out, and_4_out, and_5_out, and_6_out, and_7_out, and_8_out, and_9_out,
       and_10_out, not_1_out, not_2_out, not_3_out, not_4_out, or_1_out, or_2_out, or_3_out, or_4_out;

  not not_1 (not_1_out, A);
  not not_2 (not_2_out, B);
  not not_3 (not_3_out, C);
  not not_4 (not_4_out, D);
  and and_1 (and_1_out, not_1_out, not_2_out, C, not_4_out);
  and and_2 (and_2_out, not_1_out, not_2_out, C, D);
  and and_3 (and_3_out, not_1_out, B, not_3_out, D);
  and and_4 (and_4_out, not_1_out, B, C, D);
  and and_5 (and_5_out, A, not_2_out, C, D);
  and and_6 (and_6_out, A, B, not_3_out, D);
  and and_7 (and_7_out, not_2_out, not_1_out, C);
  and and_8 (and_8_out, not_2_out, C, D);
  and and_9 (and_9_out, B, not_3_out, D);
  and and_10 (and_10_out, not_1_out, B, D);
  or or_1 (or_1_out, B, C);
  or or_2 (or_2_out, not_2_out, D);
  or or_3 (or_3_out, not_1_out, not_2_out, not_3_out);
  or or_4 (or_4_out, not_1_out, not_3_out, D);
  or u_F_Can (F_can, and_1_out, and_2_out, and_3_out, and_4_out, and_5_out, and_6_out);
  or u_F_sop (F_sop, and_7_out, and_8_out, and_9_out, and_10_out);
  and u_F_pos (F_pos, or_1_out, or_2_out, or_3_out, or_4_out);
  nor u_EQ1 (EQ1, F_can, F_sop);
  nor u_EQ2 (EQ2, F_can, F_pos);
endmodule

module TN5 (
  input  in_1,
  input  in_2,
  input  in_3,
  output out_4
);

  wire xor_1_out;

  xor xor_1 (xor_1_out, in_1, in_2);
  xor xor_2 (out_4, xor_1_out, in_3);
endmodule
